// Logisim project toyCPU.circ as structural Verilog: 4 circuits, main circuit main
module main (
  input  [7:0] I,
  input  S,
  input  E,
  output [7:0] O
);

  wire [7:0] cpu_mem_8_1_o;

  CPU_MEM_8 cpu_mem_8_1 (.I(I), .S(S), .O(cpu_mem_8_1_o));
  CPU_ENABLE cpu_enable_1 (.I(cpu_mem_8_1_o), .E(E), .O(O));
endmodule

module CPU_MEM_1 (
  input  I,
  input  S,
  output Q
);

  wire nand_1_out, nand_2_out, nand_4_out;

  nand nand_1 (nand_1_out, I, S);
  nand nand_2 (nand_2_out, nand_1_out, S);
  nand nand_3 (Q, nand_1_out, nand_4_out);
  nand nand_4 (nand_4_out, Q, nand_2_out);
endmodule

module CPU_MEM_8 (
  input  [7:0] I,
  input  S,
  output [7:0] O
);

  CPU_MEM_1 cpu_mem_1_1 (.I(I[0]), .S(S), .Q(O[0]));
  CPU_MEM_1 cpu_mem_1_2 (.I(I[1]), .S(S), .Q(O[1]));
  CPU_MEM_1 cpu_mem_1_3 (.I(I[2]), .S(S), .Q(O[2]));
  CPU_MEM_1 cpu_mem_1_4 (.I(I[3]), .S(S), .Q(O[3]));
  CPU_MEM_1 cpu_mem_1_5 (.I(I[4]), .S(S), .Q(O[4]));
  CPU_MEM_1 cpu_mem_1_6 (.I(I[5]), .S(S), .Q(O[5]));
  CPU_MEM_1 cpu_mem_1_7 (.I(I[6]), .S(S), .Q(O[6]));
  CPU_MEM_1 cpu_mem_1_8 (.I(I[7]), .S(S), .Q(O[7]));
endmodule

module CPU_ENABLE (
  input  [7:0] I,
  input  E,
  output [7:0] O
);

  and and_1 (O[0], I[0], E);
  and and_2 (O[1], I[1], E);
  and and_3 (O[2], I[2], E);
  and and_4 (O[3], I[3], E);
  and and_5 (O[4], I[4], E);
  and and_6 (O[5], I[5], E);
  and and_7 (O[6], I[6], E);
  and and_8 (O[7], I[7], E);
endmodule
